// Logisim project ex2.circ as structural Verilog: 6 circuits, main circuit AND2
module AND2 (
  input  A,
  input  B,
  output RESULT
);

  and and_1 (RESULT, A, B);

  // Notes on the sheet:
  //   Sample Circuit
endmodule

module NAND2 (
  input  A,
  input  B,
  output RESULT
);

  wire and2_1_result;

  not not_1 (RESULT, and2_1_result);
  AND2 and2_1 (.A(A), .B(B), .RESULT(and2_1_result));
endmodule

module NOR2 (
  input  A,
  input  B,
  output RESULT
);

  wire or_1_out;

  or or_1 (or_1_out, A, B);
  not not_1 (RESULT, or_1_out);
endmodule

module XOR2 (
  input  A,
  input  B,
  output RESULT
);

  wire and2_1_result, and2_2_result, not_1_out, not_2_out;

  not not_1 (not_1_out, B);
  not not_2 (not_2_out, A);
  AND2 and2_1 (.A(A), .B(not_1_out), .RESULT(and2_1_result));
  AND2 and2_2 (.A(not_2_out), .B(B), .RESULT(and2_2_result));
  or or_1 (RESULT, and2_1_result, and2_2_result);
endmodule

module MUX2 (
  input  A,
  input  B,
  input  SEL,
  output RESULT
);

  wire and2_1_result, and2_2_result, not_1_out;

  not not_1 (not_1_out, SEL);
  AND2 and2_1 (.A(A), .B(not_1_out), .RESULT(and2_1_result));
  AND2 and2_2 (.A(B), .B(SEL), .RESULT(and2_2_result));
  or or_1 (RESULT, and2_1_result, and2_2_result);
endmodule

module MUX4 (
  input  A,
  input  B,
  input  C,
  input  D,
  input  SEL0,
  input  SEL1,
  output RESULT
);

  wire and_1_out, and_2_out, and_3_out, and_4_out, and_5_out, and_6_out, not_1_out, not_2_out, or_1_out,
       or_2_out;

  not not_1 (not_1_out, SEL1);
  and and_1 (and_1_out, A, not_1_out);
  and and_2 (and_2_out, B, not_1_out);
  and and_3 (and_3_out, C, SEL1);
  and and_4 (and_4_out, D, SEL1);
  or or_1 (or_1_out, and_2_out, and_4_out);
  or or_2 (or_2_out, and_1_out, and_3_out);
  not not_2 (not_2_out, SEL0);
  and and_5 (and_5_out, or_1_out, SEL0);
  and and_6 (and_6_out, or_2_out, not_2_out);
  or or_3 (RESULT, and_5_out, and_6_out);
endmodule
